# Fritzing sketch Melrose_box_Scheme (saved by Fritzing 0.8.3b)
breadboards: 1

parts:
  GLCD_128x1 = 128 x 64 Graphic LCD
  Part1 = Arduino Uno (Rev3)
  Left = Pushbutton [package="[THT]"]
  Right = Pushbutton [package="[THT]"]
  Down = Pushbutton [package="[THT]"]
  Up = Pushbutton [package="[THT]"]
  R1 = Resistor [tolerance=±5% resistance=10k package=THT]
  R2 = Resistor [tolerance=±5% resistance=10k package=THT]
  R3 = Resistor [tolerance=±5% resistance=10k package=THT]
  R4 = Resistor [tolerance=±5% resistance=10k package=THT]

nets:
  N1: GLCD_128x1.1_Vss, GLCD_128x1.20_K(-), Part1.GND, R1.Pin_1, R2.Pin_1, R3.Pin_1, R4.Pin_1
  N2: GLCD_128x1.2_Vdd, GLCD_128x1.15_CS1, GLCD_128x1.17_RST, GLCD_128x1.19_A(+), Part1.5V, Left.Pin_1, Left.Pin_2, Right.Pin_1, Right.Pin_2, Down.Pin_1, Down.Pin_2, Up.Pin_1, Up.Pin_2
  N3: GLCD_128x1.3_Vo, Part1.ICSP_MOSI, Part1.D11_PWM/MOSI
  N4: GLCD_128x1.4_D/I, Part1.D2
  N5: GLCD_128x1.5_R/W, Part1.D3_PWM
  N6: GLCD_128x1.6_Enable, Part1.D1/TX
  N7: GLCD_128x1.7_DB0, Part1.D8
  N8: GLCD_128x1.8_DB1, Part1.D9_PWM
  N9: GLCD_128x1.9_BD2, Part1.D10_PWM/SS
  N10: GLCD_128x1.10_DB3, Part1.ICSP_MISO, Part1.D12/MISO
  N11: GLCD_128x1.11_DB4, Part1.D4
  N12: GLCD_128x1.12_DB5, Part1.D5_PWM
  N13: GLCD_128x1.13_DB6, Part1.D6_PWM
  N14: GLCD_128x1.14_DB7, Part1.D7
  N15: Part1.A0, Left.Pin_3, Left.Pin_4, R1.Pin_0
  N16: Part1.A1, Right.Pin_3, Right.Pin_4, R2.Pin_0
  N17: Part1.A2, Down.Pin_3, Down.Pin_4, R3.Pin_0
  N18: Part1.A3, Up.Pin_3, Up.Pin_4, R4.Pin_0
